# Fritzing sketch fritzing (saved by Fritzing 0.9.2b)
circuit board: 8.46667cm x 5.64444cm
breadboards: 1

parts:
  Bauteil4 = Arduino Micro (Rev3)
  Q1 = MOSFET-NCHANNEL [package=to-92]
  J1 = female pin header, 5 pins [form="♀ (female)"]
  J2 = double row female pin header, 10 pins [form="♀ (female)"]
  Q2 = MOSFET-NCHANNEL [package=to-92]
  Q3 = MOSFET-NCHANNEL [package=to-92]
  Q4 = MOSFET-NCHANNEL [package=to-92]
  Q5 = MOSFET-NCHANNEL [package=to-92]

nets:
  N1: Bauteil4.GND, Q1.G, J1.pin1, Q2.G, Q3.G, Q4.G, Q5.G
  N2: Bauteil4.D2/SDA, Q5.S
  N3: Bauteil4.D3/SCL, Q4.S
  N4: Bauteil4.D4_PWM/A6, Q3.S
  N5: Bauteil4.D5_PWM, Q2.S
  N6: Bauteil4.D6_PWM/A7, Q1.S
  N7: Bauteil4.D7, J2.pin4
  N8: Bauteil4.D8_PWM/A8, J2.pin5
  N9: Bauteil4.D9_PWM/A9, J2.pin6
  N10: Bauteil4.D11_PWM, J1.pin5
  N11: Bauteil4.D12_PWM/A11, J1.pin3
  N12: Bauteil4.5V, J1.pin2, J2.pin1
  N13: Q1.D, J2.pin2
  N14: J2.pin3, Q3.D
  N15: J2.pin7, Q4.D
  N16: J2.pin8, Q2.D
  N17: J2.pin9, Q5.D
